// Logisim project ULA.circ as structural Verilog: 5 circuits, main circuit main
module main (
  input  A7,
  input  A6,
  input  A5,
  input  A4,
  input  A3,
  input  A2,
  input  A1,
  input  A0,
  input  SUB,
  input  Enable,
  input  B7,
  input  B6,
  input  B5,
  input  B4,
  input  B3,
  input  B2,
  input  B1,
  input  B0,
  output Overflow
);

  wire Clock_out, R1_s0, R1_s1, R1_s2, R1_s3, R1_s4, R1_s5, R1_s6, R1_s7, R2_s0, R2_s1, R2_s2, R2_s3, R2_s4,
       R2_s5, R2_s6, R2_s7, ULA_s0, ULA_s1, ULA_s2, ULA_s3, ULA_s4, ULA_s5, ULA_s6, ULA_s7;

  Clock Clock (.out(Clock_out));
  _8bit_reg R1 (
    .Clock(Clock_out), .Enable(Enable), .D7(A7), .D6(A6), .D5(A5), .D4(A4), .D3(A3), .D2(A2), .D1(A1),
    .D0(A0), .S7(R1_s7), .S6(R1_s6), .S5(R1_s5), .S4(R1_s4), .S3(R1_s3), .S2(R1_s2), .S1(R1_s1), .S0(R1_s0));
  _8bit_adder ULA (
    .INV(SUB), .PLUS1(SUB), .OVERFLOW(Overflow), .A7(R1_s7), .A6(R1_s6), .A5(R1_s5), .A4(R1_s4), .A3(R1_s3),
    .A2(R1_s2), .A1(R1_s1), .A0(R1_s0), .S7(ULA_s7), .B7(R2_s0), .S6(ULA_s6), .B6(R2_s1), .S5(ULA_s5),
    .B5(R2_s2), .S4(ULA_s4), .B4(R2_s3), .S3(ULA_s3), .B3(R2_s4), .S2(ULA_s2), .B2(R2_s5), .S1(ULA_s1),
    .B1(R2_s6), .S0(ULA_s0), .B0(R2_s7));
  _8bit_reg R2 (
    .Clock(Clock_out), .Enable(Enable), .D7(B0), .D6(B1), .D5(B2), .D4(B3), .D3(B4), .D2(B5), .D1(B6),
    .D0(B7), .S7(R2_s7), .S6(R2_s6), .S5(R2_s5), .S4(R2_s4), .S3(R2_s3), .S2(R2_s2), .S1(R2_s1), .S0(R2_s0));
  DotMatrix #(.matrixcols(8), .matrixrows(1), .dotshape("circle")) dotmatrix_1 (
    .col0(ULA_s7), .col1(ULA_s6), .col2(ULA_s5), .col3(ULA_s4), .col4(ULA_s3), .col5(ULA_s2), .col6(ULA_s1),
    .col7(ULA_s0));
endmodule

module full_adder (
  input  A,
  input  Carry_In,
  input  B,
  output Carry_Out,
  output S
);

  wire and_1_out, and_2_out, xor_1_out;

  xor xor_1 (xor_1_out, A, B);
  xor xor_2 (S, xor_1_out, Carry_In);
  or or_1 (Carry_Out, and_1_out, and_2_out);
  and and_1 (and_1_out, Carry_In, B);
  and and_2 (and_2_out, A, B);
endmodule

module _8bit_adder (
  input  A7,
  input  A6,
  input  A5,
  input  A4,
  input  A3,
  input  A2,
  input  A1,
  input  A0,
  input  INV,
  input  PLUS1,
  input  B7,
  input  B6,
  input  B5,
  input  B4,
  input  B3,
  input  B2,
  input  B1,
  input  B0,
  output OVERFLOW,
  output S7,
  output S6,
  output S5,
  output S4,
  output S3,
  output S2,
  output S1,
  output S0
);

  wire full_adder_2_carry_out, full_adder_3_carry_out, full_adder_4_carry_out, full_adder_5_carry_out,
       full_adder_6_carry_out, full_adder_7_carry_out, full_adder_8_carry_out, inverter_1_s1, inverter_2_s1,
       inverter_3_s1, inverter_4_s1, inverter_5_s1, inverter_6_s1, inverter_7_s1, inverter_8_s1;

  inverter inverter_1 (.IN(A7), .INV(INV), .S1(inverter_1_s1));
  inverter inverter_2 (.IN(A6), .INV(INV), .S1(inverter_2_s1));
  full_adder full_adder_1 (.Carry_Out(OVERFLOW), .S(S7), .A(inverter_1_s1), .B(B7), .Carry_In(full_adder_3_carry_out));
  inverter inverter_3 (.IN(A5), .INV(INV), .S1(inverter_3_s1));
  full_adder full_adder_2 (
    .Carry_Out(full_adder_2_carry_out), .S(S5), .A(inverter_3_s1), .B(B5), .Carry_In(full_adder_4_carry_out));
  full_adder full_adder_3 (
    .Carry_Out(full_adder_3_carry_out), .S(S6), .A(inverter_2_s1), .B(B6), .Carry_In(full_adder_2_carry_out));
  inverter inverter_4 (.IN(A4), .INV(INV), .S1(inverter_4_s1));
  full_adder full_adder_4 (
    .Carry_Out(full_adder_4_carry_out), .S(S4), .A(inverter_4_s1), .B(B4), .Carry_In(full_adder_5_carry_out));
  inverter inverter_5 (.IN(A3), .INV(INV), .S1(inverter_5_s1));
  inverter inverter_6 (.IN(A2), .INV(INV), .S1(inverter_6_s1));
  full_adder full_adder_5 (
    .Carry_Out(full_adder_5_carry_out), .S(S3), .A(inverter_5_s1), .B(B3), .Carry_In(full_adder_7_carry_out));
  inverter inverter_7 (.IN(A1), .INV(INV), .S1(inverter_7_s1));
  full_adder full_adder_6 (
    .Carry_Out(full_adder_6_carry_out), .S(S1), .A(inverter_7_s1), .B(B1), .Carry_In(full_adder_8_carry_out));
  full_adder full_adder_7 (
    .Carry_Out(full_adder_7_carry_out), .S(S2), .A(inverter_6_s1), .B(B2), .Carry_In(full_adder_6_carry_out));
  inverter inverter_8 (.IN(A0), .INV(INV), .S1(inverter_8_s1));
  full_adder full_adder_8 (.Carry_Out(full_adder_8_carry_out), .S(S0), .A(inverter_8_s1), .B(B0), .Carry_In(PLUS1));
endmodule

module inverter (
  input  IN,
  input  INV,
  output S1
);

  xor xor_1 (S1, IN, INV);
endmodule

module _8bit_reg (
  input  D7,
  input  D6,
  input  D5,
  input  D4,
  input  D3,
  input  D2,
  input  D1,
  input  D0,
  input  Clock,
  input  Enable,
  output S7,
  output S6,
  output S5,
  output S4,
  output S3,
  output S2,
  output S1,
  output S0
);

  D_Flip_Flop d_ff_1 (.clk(Clock), .D(D7), .Q(S7), .en(Enable));  // open: Qn, preset, reset
  D_Flip_Flop d_ff_2 (.clk(Clock), .D(D6), .Q(S6), .en(Enable));  // open: Qn, preset, reset
  D_Flip_Flop d_ff_3 (.clk(Clock), .D(D5), .Q(S5), .en(Enable));  // open: Qn, preset, reset
  D_Flip_Flop d_ff_4 (.clk(Clock), .D(D4), .Q(S4), .en(Enable));  // open: Qn, preset, reset
  D_Flip_Flop d_ff_5 (.clk(Clock), .D(D3), .Q(S3), .en(Enable));  // open: Qn, preset, reset
  D_Flip_Flop d_ff_6 (.clk(Clock), .D(D2), .Q(S2), .en(Enable));  // open: Qn, preset, reset
  D_Flip_Flop d_ff_7 (.clk(Clock), .D(D1), .Q(S1), .en(Enable));  // open: Qn, preset, reset
  D_Flip_Flop d_ff_8 (.clk(Clock), .D(D0), .Q(S0), .en(Enable));  // open: Qn, preset, reset
endmodule
