// Logisim project console-tty.circ as structural Verilog: 1 circuit, main circuit main
module main (
  input  in_1,
  input  in_2,
  input  in_3,
  input  in_4
);

  wire clock_1_out;
  wire [6:0] counter_1_q, rom_1_data;

  Counter #(.width(7), .max('h7f)) counter_1 (
    .count(in_3), .Q(counter_1_q), .clk(clock_1_out), .clr(in_4));  // open: load, D, carry
  ROM #(.addrWidth(7), .dataWidth(7)) rom_1 (.addr(counter_1_q), .data(rom_1_data), .sel(in_1));
  Clock clock_1 (.out(clock_1_out));
  TTY tty_1 (.data(rom_1_data), .clk(clock_1_out), .clr(in_2));  // open: we
endmodule
