// Logisim project cpu2.circ as structural Verilog: 4 circuits, main circuit main
module main (
  input  [8:0] in_1,
  input  in_2,
  input  in_3,
  input  in_4,
  input  in_5,
  input  in_6,
  input  in_7,
  input  in_8,
  input  in_9,
  input  in_10,
  output out_11,
  output out_12,
  output out_13,
  output out_14,
  output out_15
);

  wire ula_2_cout, ula_3_cout, ula_4_cout;

  ULA ula_1 (
    .CE(in_1[8]), .Cin(ula_2_cout), .Bin(in_2), .INVB(in_1[7]), .Ain(in_7), .INVA(in_1[6]), .I0(in_1[5]),
    .I1(in_1[4]), .in_9(in_1[3]), .I2(in_1[2]), .I3(in_1[1]), .INVOut(in_1[0]), .Out(out_12), .Cout(out_11));
  ULA ula_2 (
    .CE(in_1[8]), .Cin(ula_3_cout), .Bin(in_3), .INVB(in_1[7]), .Ain(in_8), .INVA(in_1[6]), .I0(in_1[5]),
    .I1(in_1[4]), .in_9(in_1[3]), .I2(in_1[2]), .I3(in_1[1]), .INVOut(in_1[0]), .Out(out_13),
    .Cout(ula_2_cout));
  ULA ula_3 (
    .CE(in_1[8]), .Cin(ula_4_cout), .Bin(in_4), .INVB(in_1[7]), .Ain(in_9), .INVA(in_1[6]), .I0(in_1[5]),
    .I1(in_1[4]), .in_9(in_1[3]), .I2(in_1[2]), .I3(in_1[1]), .INVOut(in_1[0]), .Out(out_14),
    .Cout(ula_3_cout));
  ULA ula_4 (
    .CE(in_1[8]), .Cin(in_6), .Bin(in_5), .INVB(in_1[7]), .Ain(in_10), .INVA(in_1[6]), .I0(in_1[5]),
    .I1(in_1[4]), .in_9(in_1[3]), .I2(in_1[2]), .I3(in_1[1]), .INVOut(in_1[0]), .Out(out_15),
    .Cout(ula_4_cout));

  // Notes on the sheet:
  //   Definição da CPU
  //   Operações matemáticas: somar, subtrair e multiplicar inteiros.
  //   Operações lógicas: e, ou, não e, não ou, ou exclusivo, não ou exclusive, igualdade.
endmodule

module ULA (
  input  CE,
  input  Cin,
  input  Bin,
  input  INVB,
  input  Ain,
  input  INVA,
  input  I0,
  input  I1,
  input  in_9,
  input  I2,
  input  I3,
  input  INVOut,
  output Out,
  output Cout
);

  wire and_1_out, and_2_out, and_3_out, and_4_out, and_5_out, controlled_buffer_1_out,
       controlled_buffer_2_out, controlled_buffer_3_out, controlled_buffer_4_out, controlled_buffer_5_out,
       controlled_buffer_10_out, controlled_buffer_12_out, even_parity_1_out, multiplexer_1_out, nand_1_out,
       nor_1_out, odd_parity_1_out, or_1_out, or_2_out, xnor_1_out, xor_1_out, xor_2_out, xor_3_out,
       xor_4_out, xor_5_out;
  wire [3:0] controlled_buffer_6_out;

  assign controlled_buffer_1_out = CE ? Cin : 1'bz;  // Controlled_Buffer controlled_buffer_1
  assign controlled_buffer_2_out = CE ? Bin : 1'bz;  // Controlled_Buffer controlled_buffer_2
  assign controlled_buffer_3_out = CE ? INVB : 1'bz;  // Controlled_Buffer controlled_buffer_3
  assign controlled_buffer_4_out = CE ? Ain : 1'bz;  // Controlled_Buffer controlled_buffer_4
  assign controlled_buffer_5_out = CE ? INVA : 1'bz;  // Controlled_Buffer controlled_buffer_5
  assign controlled_buffer_6_out[0] = CE ? I0 : 1'bz;  // Controlled_Buffer controlled_buffer_6
  assign controlled_buffer_6_out[1] = CE ? I1 : 1'bz;  // Controlled_Buffer controlled_buffer_7
  assign controlled_buffer_6_out[2] = CE ? I2 : 1'bz;  // Controlled_Buffer controlled_buffer_8
  assign controlled_buffer_6_out[3] = CE ? I3 : 1'bz;  // Controlled_Buffer controlled_buffer_9
  assign controlled_buffer_10_out = CE ? INVOut : 1'bz;  // Controlled_Buffer controlled_buffer_10
  and and_1 (and_1_out, ~controlled_buffer_6_out[0], ~controlled_buffer_6_out[1], ~controlled_buffer_6_out[2], controlled_buffer_6_out[3]);  // AND_Gate
  xor xor_1 (xor_1_out, controlled_buffer_2_out, controlled_buffer_3_out);
  xor xor_2 (xor_2_out, controlled_buffer_4_out, controlled_buffer_5_out);
  and and_2 (and_2_out, xor_2_out, xor_1_out);
  or or_1 (or_1_out, xor_2_out, xor_1_out);
  nor nor_1 (nor_1_out, xor_2_out, xor_1_out);
  nand nand_1 (nand_1_out, xor_2_out, xor_1_out);
  Multiplexer #(.select(4)) multiplexer_1 (
    .in0(and_2_out), .in1(or_1_out), .in2(nand_1_out), .in3(nor_1_out), .in4(xor_4_out), .in5(xnor_1_out),
    .in6(odd_parity_1_out), .in7(even_parity_1_out), .in8(xor_5_out), .in9(in_9), .in10(in_9), .in11(in_9),
    .in12(in_9), .in13(in_9), .in14(in_9), .in15(in_9), .out(multiplexer_1_out),
    .sel(controlled_buffer_6_out), .en(CE));
  xor xor_3 (xor_3_out, controlled_buffer_10_out, multiplexer_1_out);
  assign Out = CE ? xor_3_out : 1'bz;  // Controlled_Buffer controlled_buffer_11
  xor xor_4 (xor_4_out, xor_2_out, xor_1_out);
  xnor xnor_1 (xnor_1_out, xor_2_out, xor_1_out);
  xor odd_parity_1 (odd_parity_1_out, xor_2_out, xor_1_out);
  xnor even_parity_1 (even_parity_1_out, xor_2_out, xor_1_out);
  and and_3 (and_3_out, xor_1_out, controlled_buffer_1_out);
  and and_4 (and_4_out, xor_2_out, controlled_buffer_1_out);
  and and_5 (and_5_out, xor_1_out, xor_2_out);
  xor xor_5 (xor_5_out, xor_1_out, controlled_buffer_1_out, xor_2_out);
  or or_2 (or_2_out, and_5_out, and_4_out, and_3_out);
  assign controlled_buffer_12_out = and_1_out ? or_2_out : 1'bz;  // Controlled_Buffer controlled_buffer_12
  assign Cout = CE ? controlled_buffer_12_out : 1'bz;  // Controlled_Buffer controlled_buffer_13
endmodule

module Decodificador_3b8 (
  input  C,
  input  B,
  input  A,
  output _111,
  output _110,
  output _101,
  output _100,
  output _011,
  output _010,
  output _001,
  output _000
);

  wire and_1_out, and_3_out, and_5_out, and_7_out, and_9_out, and_11_out, and_13_out, and_15_out;

  and and_1 (and_1_out, A, B);
  and and_2 (_111, and_1_out, C);
  and and_3 (and_3_out, ~A, B);  // AND_Gate
  and and_4 (_110, and_3_out, C);
  and and_5 (and_5_out, A, ~B);  // AND_Gate
  and and_6 (_101, and_5_out, C);
  and and_7 (and_7_out, ~A, ~B);  // AND_Gate
  and and_8 (_100, and_7_out, C);
  and and_9 (and_9_out, A, B);
  and and_10 (_011, and_9_out, ~C);  // AND_Gate
  and and_11 (and_11_out, ~A, B);  // AND_Gate
  and and_12 (_010, and_11_out, ~C);  // AND_Gate
  and and_13 (and_13_out, A, ~B);  // AND_Gate
  and and_14 (_001, and_13_out, ~C);  // AND_Gate
  and and_15 (and_15_out, ~A, ~B);  // AND_Gate
  and and_16 (_000, and_15_out, ~C);  // AND_Gate
endmodule

module Decodificador_4b16 (
  input  D,
  input  C,
  input  B,
  input  A,
  output _1111,
  output _1110,
  output _1101,
  output _1100,
  output _1011,
  output _1010,
  output _1001,
  output _1000,
  output _0111,
  output _0110,
  output _0101,
  output _0100,
  output _0011,
  output _0010,
  output _0001,
  output _0000
);

  wire and_1_out, and_2_out, and_3_out, and_4_out, and_5_out, and_6_out, and_7_out, and_8_out, and_9_out,
       and_10_out, and_11_out, and_12_out, and_13_out, and_14_out, and_15_out, and_16_out, and_17_out,
       and_19_out, and_21_out, and_23_out, and_25_out, and_27_out, and_29_out, and_31_out, and_33_out,
       and_35_out, and_37_out, and_39_out, and_41_out, and_43_out, and_45_out, and_47_out;

  and and_1 (and_1_out, A, B);
  and and_2 (and_2_out, ~A, B);  // AND_Gate
  and and_3 (and_3_out, A, ~B);  // AND_Gate
  and and_4 (and_4_out, ~A, ~B);  // AND_Gate
  and and_5 (and_5_out, A, B);
  and and_6 (and_6_out, ~A, B);  // AND_Gate
  and and_7 (and_7_out, A, ~B);  // AND_Gate
  and and_8 (and_8_out, ~A, ~B);  // AND_Gate
  and and_9 (and_9_out, A, B);
  and and_10 (and_10_out, ~A, B);  // AND_Gate
  and and_11 (and_11_out, A, ~B);  // AND_Gate
  and and_12 (and_12_out, ~A, ~B);  // AND_Gate
  and and_13 (and_13_out, A, B);
  and and_14 (and_14_out, ~A, B);  // AND_Gate
  and and_15 (and_15_out, A, ~B);  // AND_Gate
  and and_16 (and_16_out, ~A, ~B);  // AND_Gate
  and and_17 (and_17_out, and_1_out, C);
  and and_18 (_1111, and_17_out, D);
  and and_19 (and_19_out, and_2_out, C);
  and and_20 (_1110, and_19_out, D);
  and and_21 (and_21_out, and_3_out, C);
  and and_22 (_1101, and_21_out, D);
  and and_23 (and_23_out, and_4_out, C);
  and and_24 (_1100, and_23_out, D);
  and and_25 (and_25_out, and_5_out, ~C);  // AND_Gate
  and and_26 (_1011, and_25_out, D);
  and and_27 (and_27_out, and_6_out, ~C);  // AND_Gate
  and and_28 (_1010, and_27_out, D);
  and and_29 (and_29_out, and_7_out, ~C);  // AND_Gate
  and and_30 (_1001, and_29_out, D);
  and and_31 (and_31_out, and_8_out, ~C);  // AND_Gate
  and and_32 (_1000, and_31_out, D);
  and and_33 (and_33_out, and_9_out, C);
  and and_34 (_0111, and_33_out, ~D);  // AND_Gate
  and and_35 (and_35_out, and_10_out, C);
  and and_36 (_0110, and_35_out, ~D);  // AND_Gate
  and and_37 (and_37_out, and_11_out, C);
  and and_38 (_0101, and_37_out, ~D);  // AND_Gate
  and and_39 (and_39_out, and_12_out, C);
  and and_40 (_0100, and_39_out, ~D);  // AND_Gate
  and and_41 (and_41_out, and_13_out, ~C);  // AND_Gate
  and and_42 (_0011, and_41_out, ~D);  // AND_Gate
  and and_43 (and_43_out, and_14_out, ~C);  // AND_Gate
  and and_44 (_0010, and_43_out, ~D);  // AND_Gate
  and and_45 (and_45_out, and_15_out, ~C);  // AND_Gate
  and and_46 (_0001, and_45_out, ~D);  // AND_Gate
  and and_47 (and_47_out, and_16_out, ~C);  // AND_Gate
  and and_48 (_0000, and_47_out, ~D);  // AND_Gate
endmodule
