// Logisim project cpu3.circ as structural Verilog: 4 circuits, main circuit main
module main (
  input  in_1,
  input  [7:0] in_2,
  input  in_3,
  input  in_4,
  input  in_5,
  input  in_6,
  input  in_7,
  input  [7:0] in_8,
  input  in_9,
  input  in_10
);

  wire clock_1_out;
  wire [4:0] rom_1_data;
  wire [7:0] counter_1_q, counter_2_q, ram_1_data, undriven;

  Clock clock_1 (.out(clock_1_out));
  Counter counter_1 (
    .load(in_1), .D(in_2), .count(in_3), .Q(counter_1_q), .clk(clock_1_out), .clr(in_6));  // open: carry
  Counter counter_2 (
    .load(in_7), .D(in_8), .count(in_9), .Q(counter_2_q), .clk(clock_1_out), .clr(in_10));  // open: carry
  RAM ram_1 (.addr(counter_1_q), .data(ram_1_data), .sel(in_4), .clk(clock_1_out), .ld(rom_1_data[0]), .clr(in_5));
  ROM #(.dataWidth(5)) rom_1 (.addr(counter_2_q), .data(rom_1_data));  // open: sel
  DotMatrix #(.inputtype("row"), .matrixcols(8), .matrixrows(1)) dotmatrix_1 (.row0(undriven));
  ULA_Simples ula_simples_1 (
    .LOAD(rom_1_data[0]), .PLUS1(rom_1_data[1]), .TRANSFER(rom_1_data[2]), .CLR(rom_1_data[3]),
    .in_1(ram_1_data[7]), .in_2(ram_1_data[6]), .in_3(ram_1_data[5]), .in_4(ram_1_data[4]),
    .in_5(ram_1_data[3]), .in_6(ram_1_data[2]), .in_7(ram_1_data[1]), .in_8(ram_1_data[0]),
    .INV(rom_1_data[4]));  // open: OVF, out_15, out_16, out_17, out_18, out_19, out_20, out_21, out_22
endmodule

module ULA_Simples (
  input  in_1,
  input  in_2,
  input  in_3,
  input  in_4,
  input  in_5,
  input  in_6,
  input  in_7,
  input  in_8,
  input  INV,
  input  LOAD,
  input  PLUS1,
  input  TRANSFER,
  input  CLR,
  output OVF,
  output out_15,
  output out_16,
  output out_17,
  output out_18,
  output out_19,
  output out_20,
  output out_21,
  output out_22
);

  wire d_ff_1_q, d_ff_3_q, d_ff_5_q, d_ff_7_q, d_ff_9_q, d_ff_11_q, d_ff_13_q, d_ff_15_q, somador_1_out_5,
       somador_2_out_4, somador_2_out_5, somador_3_out_4, somador_3_out_5, somador_4_out_4, somador_4_out_5,
       somador_5_out_4, somador_5_out_5, somador_6_out_4, somador_6_out_5, somador_7_out_4, somador_7_out_5,
       somador_8_out_4, somador_8_out_5, xor_1_out, xor_2_out, xor_3_out, xor_4_out, xor_5_out, xor_6_out,
       xor_7_out, xor_8_out;

  xor xor_1 (xor_1_out, INV, in_1);
  D_Flip_Flop d_ff_1 (.clk(LOAD), .D(xor_1_out), .Q(d_ff_1_q), .en(1'b1));  // open: Qn, preset, reset
  D_Flip_Flop d_ff_2 (.clk(TRANSFER), .D(somador_1_out_5), .Q(out_15), .en(1'b1), .reset(CLR));  // open: Qn, preset
  xor xor_2 (xor_2_out, INV, in_2);
  D_Flip_Flop d_ff_3 (.clk(LOAD), .D(xor_2_out), .Q(d_ff_3_q), .en(1'b1));  // open: Qn, preset, reset
  Somador somador_1 (.out_4(OVF), .out_5(somador_1_out_5), .in_1(d_ff_1_q), .in_3(out_15), .in_2(somador_2_out_4));
  D_Flip_Flop d_ff_4 (.clk(TRANSFER), .D(somador_2_out_5), .Q(out_16), .en(1'b1), .reset(CLR));  // open: Qn, preset
  xor xor_3 (xor_3_out, INV, in_3);
  D_Flip_Flop d_ff_5 (.clk(LOAD), .D(xor_3_out), .Q(d_ff_5_q), .en(1'b1));  // open: Qn, preset, reset
  Somador somador_2 (
    .out_4(somador_2_out_4), .out_5(somador_2_out_5), .in_1(d_ff_3_q), .in_3(out_16), .in_2(somador_3_out_4));
  D_Flip_Flop d_ff_6 (.clk(TRANSFER), .D(somador_3_out_5), .Q(out_17), .en(1'b1), .reset(CLR));  // open: Qn, preset
  xor xor_4 (xor_4_out, INV, in_4);
  Somador somador_3 (
    .out_4(somador_3_out_4), .out_5(somador_3_out_5), .in_1(d_ff_5_q), .in_3(out_17), .in_2(somador_4_out_4));
  xor xor_5 (xor_5_out, INV, in_5);
  D_Flip_Flop d_ff_7 (.clk(LOAD), .D(xor_4_out), .Q(d_ff_7_q), .en(1'b1));  // open: Qn, preset, reset
  Somador somador_4 (
    .out_4(somador_4_out_4), .out_5(somador_4_out_5), .in_1(d_ff_7_q), .in_3(out_18), .in_2(somador_5_out_4));
  D_Flip_Flop d_ff_8 (.clk(TRANSFER), .D(somador_4_out_5), .Q(out_18), .en(1'b1), .reset(CLR));  // open: Qn, preset
  xor xor_6 (xor_6_out, INV, in_6);
  D_Flip_Flop d_ff_9 (.clk(LOAD), .D(xor_5_out), .Q(d_ff_9_q), .en(1'b1));  // open: Qn, preset, reset
  Somador somador_5 (
    .out_4(somador_5_out_4), .out_5(somador_5_out_5), .in_1(d_ff_9_q), .in_3(out_19), .in_2(somador_6_out_4));
  D_Flip_Flop d_ff_10 (.clk(TRANSFER), .D(somador_5_out_5), .Q(out_19), .en(1'b1), .reset(CLR));  // open: Qn, preset
  xor xor_7 (xor_7_out, INV, in_7);
  D_Flip_Flop d_ff_11 (.clk(LOAD), .D(xor_6_out), .Q(d_ff_11_q), .en(1'b1));  // open: Qn, preset, reset
  Somador somador_6 (
    .out_4(somador_6_out_4), .out_5(somador_6_out_5), .in_1(d_ff_11_q), .in_3(out_20), .in_2(somador_7_out_4));
  D_Flip_Flop d_ff_12 (.clk(TRANSFER), .D(somador_6_out_5), .Q(out_20), .en(1'b1), .reset(CLR));  // open: Qn, preset
  xor xor_8 (xor_8_out, INV, in_8);
  D_Flip_Flop d_ff_13 (.clk(LOAD), .D(xor_7_out), .Q(d_ff_13_q), .en(1'b1));  // open: Qn, preset, reset
  Somador somador_7 (
    .out_4(somador_7_out_4), .out_5(somador_7_out_5), .in_1(d_ff_13_q), .in_3(out_21), .in_2(somador_8_out_4));
  D_Flip_Flop d_ff_14 (.clk(TRANSFER), .D(somador_7_out_5), .Q(out_21), .en(1'b1), .reset(CLR));  // open: Qn, preset
  D_Flip_Flop d_ff_15 (.clk(LOAD), .D(xor_8_out), .Q(d_ff_15_q), .en(1'b1));  // open: Qn, preset, reset
  Somador somador_8 (.out_4(somador_8_out_4), .out_5(somador_8_out_5), .in_1(d_ff_15_q), .in_3(out_22), .in_2(PLUS1));
  D_Flip_Flop d_ff_16 (.clk(TRANSFER), .D(somador_8_out_5), .Q(out_22), .en(1'b1), .reset(CLR));  // open: Qn, preset
endmodule

module Somador (
  input  in_1,
  input  in_2,
  input  in_3,
  output out_4,
  output out_5
);

  wire and_1_out, and_2_out, and_3_out;

  or or_1 (out_4, and_1_out, and_2_out, and_3_out);
  xor xor_1 (out_5, in_2, in_1, in_3);
  and and_1 (and_1_out, in_2, in_1);
  and and_2 (and_2_out, in_2, in_3);
  and and_3 (and_3_out, in_1, in_3);
endmodule

module ULA_DEFEITO (
  input  in_1,
  input  in_2,
  input  in_3,
  input  in_4,
  input  in_5,
  input  in_6,
  input  in_7,
  input  in_8,
  input  LOAD,
  input  PLUS1,
  input  TRANSFER,
  input  CLR,
  input  in_13,
  input  in_14,
  input  in_15,
  input  in_16,
  input  in_17,
  input  in_18,
  input  in_19,
  input  in_20,
  output OVF,
  output out_22,
  output out_23,
  output out_24,
  output out_25,
  output out_26,
  output out_27,
  output out_28,
  output out_29
);

  wire d_ff_1_q, d_ff_2_q, d_ff_3_q, d_ff_4_q, d_ff_5_q, d_ff_6_q, d_ff_7_q, d_ff_8_q, d_ff_9_q, d_ff_10_q,
       d_ff_11_q, d_ff_12_q, d_ff_13_q, d_ff_14_q, d_ff_15_q, d_ff_16_q, somador_2_out_4, somador_3_out_4,
       somador_4_out_4, somador_5_out_4, somador_6_out_4, somador_7_out_4, somador_8_out_4;

  D_Flip_Flop d_ff_1 (.clk(LOAD), .D(in_1), .Q(d_ff_1_q), .en(1'b1));  // open: Qn, preset, reset
  D_Flip_Flop d_ff_2 (.clk(TRANSFER), .D(in_13), .Q(d_ff_2_q), .en(1'b1), .reset(CLR));  // open: Qn, preset
  D_Flip_Flop d_ff_3 (.clk(LOAD), .D(in_2), .Q(d_ff_3_q), .en(1'b1));  // open: Qn, preset, reset
  Somador somador_1 (.out_4(OVF), .out_5(out_22), .in_1(d_ff_1_q), .in_3(d_ff_2_q), .in_2(somador_2_out_4));
  D_Flip_Flop d_ff_4 (.clk(TRANSFER), .D(in_14), .Q(d_ff_4_q), .en(1'b1), .reset(CLR));  // open: Qn, preset
  D_Flip_Flop d_ff_5 (.clk(LOAD), .D(in_3), .Q(d_ff_5_q), .en(1'b1));  // open: Qn, preset, reset
  Somador somador_2 (.out_4(somador_2_out_4), .out_5(out_23), .in_1(d_ff_3_q), .in_3(d_ff_4_q), .in_2(somador_3_out_4));
  D_Flip_Flop d_ff_6 (.clk(TRANSFER), .D(in_15), .Q(d_ff_6_q), .en(1'b1), .reset(CLR));  // open: Qn, preset
  Somador somador_3 (.out_4(somador_3_out_4), .out_5(out_24), .in_1(d_ff_5_q), .in_3(d_ff_6_q), .in_2(somador_4_out_4));
  D_Flip_Flop d_ff_7 (.clk(LOAD), .D(in_4), .Q(d_ff_7_q), .en(1'b1));  // open: Qn, preset, reset
  Somador somador_4 (.out_4(somador_4_out_4), .out_5(out_25), .in_1(d_ff_7_q), .in_3(d_ff_8_q), .in_2(somador_5_out_4));
  D_Flip_Flop d_ff_8 (.clk(TRANSFER), .D(in_16), .Q(d_ff_8_q), .en(1'b1), .reset(CLR));  // open: Qn, preset
  D_Flip_Flop d_ff_9 (.clk(LOAD), .D(in_5), .Q(d_ff_9_q), .en(1'b1));  // open: Qn, preset, reset
  Somador somador_5 (
    .out_4(somador_5_out_4), .out_5(out_26), .in_1(d_ff_9_q), .in_3(d_ff_10_q), .in_2(somador_6_out_4));
  D_Flip_Flop d_ff_10 (.clk(TRANSFER), .D(in_17), .Q(d_ff_10_q), .en(1'b1), .reset(CLR));  // open: Qn, preset
  D_Flip_Flop d_ff_11 (.clk(LOAD), .D(in_6), .Q(d_ff_11_q), .en(1'b1));  // open: Qn, preset, reset
  Somador somador_6 (
    .out_4(somador_6_out_4), .out_5(out_27), .in_1(d_ff_11_q), .in_3(d_ff_12_q), .in_2(somador_7_out_4));
  D_Flip_Flop d_ff_12 (.clk(TRANSFER), .D(in_18), .Q(d_ff_12_q), .en(1'b1), .reset(CLR));  // open: Qn, preset
  D_Flip_Flop d_ff_13 (.clk(LOAD), .D(in_7), .Q(d_ff_13_q), .en(1'b1));  // open: Qn, preset, reset
  Somador somador_7 (
    .out_4(somador_7_out_4), .out_5(out_28), .in_1(d_ff_13_q), .in_3(d_ff_14_q), .in_2(somador_8_out_4));
  D_Flip_Flop d_ff_14 (.clk(TRANSFER), .D(in_19), .Q(d_ff_14_q), .en(1'b1), .reset(CLR));  // open: Qn, preset
  D_Flip_Flop d_ff_15 (.clk(LOAD), .D(in_8), .Q(d_ff_15_q), .en(1'b1));  // open: Qn, preset, reset
  Somador somador_8 (.out_4(somador_8_out_4), .out_5(out_29), .in_1(d_ff_15_q), .in_3(d_ff_16_q), .in_2(PLUS1));
  D_Flip_Flop d_ff_16 (.clk(TRANSFER), .D(in_20), .Q(d_ff_16_q), .en(1'b1), .reset(CLR));  // open: Qn, preset
endmodule
