// Logisim project SAP1.circ as structural Verilog: 3 circuits, main circuit program-counter
module program_counter (
  input  Cp,
  input  CLK,
  input  CLR,
  input  EP,
  output O3,
  output O2,
  output O1,
  output O0
);

  wire j_k_ff_1_qn, j_k_ff_2_q, j_k_ff_2_qn, j_k_ff_3_q, j_k_ff_3_qn, j_k_ff_4_q, j_k_ff_4_qn;

  // Buffer buffer_1 is placed but not wired
  J_K_Flip_Flop j_k_ff_1 (
    .J(Cp), .clk(j_k_ff_2_q), .K(Cp), .Qn(j_k_ff_1_qn), .en(1'b1), .reset(CLR));  // open: Q, preset
  assign O3 = EP ? j_k_ff_1_qn : 1'bz;  // Controlled_Buffer controlled_buffer_1
  J_K_Flip_Flop j_k_ff_2 (
    .J(Cp), .clk(j_k_ff_3_q), .K(Cp), .Q(j_k_ff_2_q), .Qn(j_k_ff_2_qn), .en(1'b1), .reset(CLR));  // open: preset
  assign O2 = EP ? j_k_ff_2_qn : 1'bz;  // Controlled_Buffer controlled_buffer_2
  J_K_Flip_Flop j_k_ff_3 (
    .J(Cp), .clk(j_k_ff_4_q), .K(Cp), .Q(j_k_ff_3_q), .Qn(j_k_ff_3_qn), .en(1'b1), .reset(CLR));  // open: preset
  assign O1 = EP ? j_k_ff_3_qn : 1'bz;  // Controlled_Buffer controlled_buffer_3
  J_K_Flip_Flop j_k_ff_4 (
    .J(Cp), .clk(CLK), .K(Cp), .Q(j_k_ff_4_q), .Qn(j_k_ff_4_qn), .en(1'b1), .reset(CLR));  // open: preset
  assign O0 = EP ? j_k_ff_4_qn : 1'bz;  // Controlled_Buffer controlled_buffer_4
endmodule

module main (
  input  CLR,
  input  EP,
  input  CP,
  input  LM
);

  wire clock_1_out, program_counter_1_o0, program_counter_1_o1, program_counter_1_o2, program_counter_1_o3;

  Clock clock_1 (.out(clock_1_out));
  program_counter program_counter_1 (
    .Cp(CP), .CLK(clock_1_out), .CLR(CLR), .O3(program_counter_1_o3), .O2(program_counter_1_o2),
    .O1(program_counter_1_o1), .O0(program_counter_1_o0), .EP(EP));
  _74LS173 u_74ls173_1 (
    ._09(LM), ._10(LM), ._07(clock_1_out), ._15(1'b0), ._01(1'b0), ._02(1'b0), ._3(program_counter_1_o3),
    ._4(program_counter_1_o2), ._5(program_counter_1_o1), ._6(program_counter_1_o0));  // open: _14, _13, _12, _11
endmodule

module _74LS173 (
  input  _14,
  input  _13,
  input  _12,
  input  _11,
  input  _09,
  input  _10,
  input  _07,
  input  _15,
  input  _01,
  input  _02,
  output _3,
  output _4,
  output _5,
  output _6
);

  wire and_1_out, and_2_out, and_3_out, and_4_out, and_5_out, and_6_out, and_7_out, and_8_out, and_9_out,
       and_10_out, d_ff_1_q, d_ff_1_qn, d_ff_2_q, d_ff_2_qn, d_ff_3_q, d_ff_3_qn, d_ff_4_q, d_ff_4_qn,
       not_1_out;

  and and_1 (and_1_out, ~_09, ~_10);  // AND_Gate
  and and_2 (and_2_out, ~_01, ~_02);  // AND_Gate
  not not_1 (not_1_out, and_1_out);
  and and_3 (and_3_out, _14, and_1_out);
  and and_4 (and_4_out, not_1_out, d_ff_1_q);
  // OR_Gate or_1 has open pins: in0=and_3_out, in1=and_4_out, out=open
  D_Flip_Flop d_ff_1 (.clk(_07), .Q(d_ff_1_q), .Qn(d_ff_1_qn), .reset(_15));  // open: D, preset, en
  assign _3 = and_2_out ? ~d_ff_1_qn : 1'bz;  // Controlled_Inverter controlled_inverter_1
  and and_5 (and_5_out, _13, and_1_out);
  and and_6 (and_6_out, not_1_out, d_ff_2_q);
  // OR_Gate or_2 has open pins: in0=and_5_out, in1=and_6_out, out=open
  D_Flip_Flop d_ff_2 (.clk(_07), .Q(d_ff_2_q), .Qn(d_ff_2_qn), .reset(_15));  // open: D, preset, en
  assign _4 = and_2_out ? ~d_ff_2_qn : 1'bz;  // Controlled_Inverter controlled_inverter_2
  and and_7 (and_7_out, _12, and_1_out);
  // OR_Gate or_3 has open pins: in0=and_7_out, in1=and_8_out, out=open
  D_Flip_Flop d_ff_3 (.clk(_07), .Q(d_ff_3_q), .Qn(d_ff_3_qn), .reset(_15));  // open: D, preset, en
  and and_8 (and_8_out, not_1_out, d_ff_3_q);
  assign _5 = and_2_out ? ~d_ff_3_qn : 1'bz;  // Controlled_Inverter controlled_inverter_3
  and and_9 (and_9_out, _11, and_1_out);
  and and_10 (and_10_out, not_1_out, d_ff_4_q);
  // OR_Gate or_4 has open pins: in0=and_9_out, in1=and_10_out, out=open
  D_Flip_Flop d_ff_4 (.clk(_07), .Q(d_ff_4_q), .Qn(d_ff_4_qn), .reset(_15));  // open: D, preset, en
  assign _6 = and_2_out ? ~d_ff_4_qn : 1'bz;  // Controlled_Inverter controlled_inverter_4
endmodule
