// Logisim project cpu1.circ as structural Verilog
module Somador_02_bits (
  input  B,
  input  Cin,
  input  A,
  output Cout,
  output S
);

  wire and_1_out, and_2_out, and_3_out;

  and and_1 (and_1_out, A, B);
  and and_2 (and_2_out, A, Cin);
  or or_1 (Cout, and_1_out, and_2_out, and_3_out);
  and and_3 (and_3_out, Cin, B);
  xor xor_1 (S, Cin, B, A);
endmodule

module Somador_08_bits (
  input  PLUS1,
  input  B7,
  input  B6,
  input  B5,
  input  B4,
  input  B3,
  input  B2,
  input  B1,
  input  B0,
  input  INVB,
  input  INVA,
  input  A7,
  input  A6,
  input  A5,
  input  A4,
  input  A3,
  input  A2,
  input  A1,
  input  A0,
  input  INVO,
  output OVF,
  output S7,
  output S6,
  output S5,
  output S4,
  output S3,
  output S2,
  output S1,
  output S0
);

  wire somador_02_bits_2_cout, somador_02_bits_2_s, somador_02_bits_3_cout, somador_02_bits_3_s,
       somador_02_bits_4_cout, somador_02_bits_4_s, somador_02_bits_5_cout, somador_02_bits_5_s,
       somador_02_bits_6_cout, somador_02_bits_6_s, somador_02_bits_7_cout, somador_02_bits_7_s,
       somador_02_bits_8_cout, somador_02_bits_8_s, xor_2_out, xor_3_out, xor_5_out, xor_7_out, xor_8_out,
       xor_10_out, xor_11_out, xor_12_out, xor_14_out, xor_16_out, xor_17_out, xor_18_out, xor_20_out,
       xor_21_out, xor_23_out, xor_24_out;

  xor xor_1 (S7, OVF, INVO);
  xor xor_2 (xor_2_out, B7, INVB);
  xor xor_3 (xor_3_out, A7, INVA);
  Somador_02_bits somador_02_bits_1 (.Cout(OVF), .S(OVF), .Cin(somador_02_bits_2_cout), .B(xor_2_out), .A(xor_3_out));
  xor xor_4 (S6, somador_02_bits_2_s, INVO);
  xor xor_5 (xor_5_out, B6, INVB);
  Somador_02_bits somador_02_bits_2 (
    .Cout(somador_02_bits_2_cout), .S(somador_02_bits_2_s), .Cin(somador_02_bits_3_cout), .B(xor_5_out),
    .A(xor_7_out));
  xor xor_6 (S5, somador_02_bits_3_s, INVO);
  xor xor_7 (xor_7_out, A6, INVA);
  xor xor_8 (xor_8_out, B5, INVB);
  Somador_02_bits somador_02_bits_3 (
    .Cout(somador_02_bits_3_cout), .S(somador_02_bits_3_s), .Cin(somador_02_bits_4_cout), .B(xor_8_out),
    .A(xor_10_out));
  xor xor_9 (S4, somador_02_bits_4_s, INVO);
  xor xor_10 (xor_10_out, A5, INVA);
  xor xor_11 (xor_11_out, B4, INVB);
  Somador_02_bits somador_02_bits_4 (
    .Cout(somador_02_bits_4_cout), .S(somador_02_bits_4_s), .Cin(somador_02_bits_5_cout), .B(xor_11_out),
    .A(xor_12_out));
  xor xor_12 (xor_12_out, A4, INVA);
  xor xor_13 (S3, somador_02_bits_5_s, INVO);
  xor xor_14 (xor_14_out, B3, INVB);
  Somador_02_bits somador_02_bits_5 (
    .Cout(somador_02_bits_5_cout), .S(somador_02_bits_5_s), .Cin(somador_02_bits_6_cout), .B(xor_14_out),
    .A(xor_16_out));
  xor xor_15 (S2, somador_02_bits_6_s, INVO);
  xor xor_16 (xor_16_out, A3, INVA);
  xor xor_17 (xor_17_out, B2, INVB);
  xor xor_18 (xor_18_out, A2, INVA);
  Somador_02_bits somador_02_bits_6 (
    .Cout(somador_02_bits_6_cout), .S(somador_02_bits_6_s), .Cin(somador_02_bits_7_cout), .B(xor_17_out),
    .A(xor_18_out));
  xor xor_19 (S1, somador_02_bits_7_s, INVO);
  xor xor_20 (xor_20_out, B1, INVB);
  Somador_02_bits somador_02_bits_7 (
    .Cout(somador_02_bits_7_cout), .S(somador_02_bits_7_s), .Cin(somador_02_bits_8_cout), .B(xor_20_out),
    .A(xor_21_out));
  xor xor_21 (xor_21_out, A1, INVA);
  xor xor_22 (S0, somador_02_bits_8_s, INVO);
  xor xor_23 (xor_23_out, B0, INVB);
  Somador_02_bits somador_02_bits_8 (
    .Cout(somador_02_bits_8_cout), .S(somador_02_bits_8_s), .Cin(PLUS1), .B(xor_23_out), .A(xor_24_out));
  xor xor_24 (xor_24_out, A0, INVA);
endmodule

module Acumulador (
  input  AIN7,
  input  AIN6,
  input  AIN5,
  input  AIN4,
  input  AIN3,
  input  AIN2,
  input  AIN1,
  input  AIN0,
  input  INVA,
  input  TRANSFER,
  input  SETA,
  input  ENA,
  input  CLRA,
  output AOUT7,
  output AOUT6,
  output AOUT5,
  output AOUT4,
  output AOUT3,
  output AOUT2,
  output AOUT1,
  output AOUT0
);

  wire xor_1_out, xor_2_out, xor_3_out, xor_4_out, xor_5_out, xor_6_out, xor_7_out, xor_8_out;

  xor xor_1 (xor_1_out, INVA, AIN7);
  xor xor_2 (xor_2_out, INVA, AIN6);
  D_Flip_Flop d_ff_1 (.clk(TRANSFER), .D(xor_1_out), .Q(AOUT7), .preset(SETA), .en(ENA), .reset(CLRA));  // open: Qn
  xor xor_3 (xor_3_out, INVA, AIN5);
  D_Flip_Flop d_ff_2 (.clk(TRANSFER), .D(xor_2_out), .Q(AOUT6), .preset(SETA), .en(ENA), .reset(CLRA));  // open: Qn
  xor xor_4 (xor_4_out, INVA, AIN4);
  D_Flip_Flop d_ff_3 (.clk(TRANSFER), .D(xor_3_out), .Q(AOUT5), .preset(SETA), .en(ENA), .reset(CLRA));  // open: Qn
  xor xor_5 (xor_5_out, INVA, AIN3);
  D_Flip_Flop d_ff_4 (.clk(TRANSFER), .D(xor_4_out), .Q(AOUT4), .preset(SETA), .en(ENA), .reset(CLRA));  // open: Qn
  xor xor_6 (xor_6_out, INVA, AIN2);
  D_Flip_Flop d_ff_5 (.clk(TRANSFER), .D(xor_5_out), .Q(AOUT3), .preset(SETA), .en(ENA), .reset(CLRA));  // open: Qn
  xor xor_7 (xor_7_out, INVA, AIN1);
  D_Flip_Flop d_ff_6 (.clk(TRANSFER), .D(xor_6_out), .Q(AOUT2), .preset(SETA), .en(ENA), .reset(CLRA));  // open: Qn
  xor xor_8 (xor_8_out, INVA, AIN0);
  D_Flip_Flop d_ff_7 (.clk(TRANSFER), .D(xor_7_out), .Q(AOUT1), .preset(SETA), .en(ENA), .reset(CLRA));  // open: Qn
  D_Flip_Flop d_ff_8 (.clk(TRANSFER), .D(xor_8_out), .Q(AOUT0), .preset(SETA), .en(ENA), .reset(CLRA));  // open: Qn
endmodule

module B (
  input  BIN7,
  input  BIN6,
  input  BIN5,
  input  BIN4,
  input  BIN3,
  input  BIN2,
  input  BIN1,
  input  BIN0,
  input  INVB,
  input  LOAD,
  input  SETB,
  input  ENB,
  input  CLRB,
  output BOUT7,
  output BOUT6,
  output BOUT5,
  output BOUT4,
  output BOUT3,
  output BOUT2,
  output BOUT1,
  output BOUT0
);

  wire xor_1_out, xor_2_out, xor_3_out, xor_4_out, xor_5_out, xor_6_out, xor_7_out, xor_8_out;

  xor xor_1 (xor_1_out, INVB, BIN7);
  xor xor_2 (xor_2_out, INVB, BIN6);
  D_Flip_Flop d_ff_1 (.clk(LOAD), .D(xor_1_out), .Q(BOUT7), .preset(SETB), .en(ENB), .reset(CLRB));  // open: Qn
  xor xor_3 (xor_3_out, INVB, BIN5);
  D_Flip_Flop d_ff_2 (.clk(LOAD), .D(xor_2_out), .Q(BOUT6), .preset(SETB), .en(ENB), .reset(CLRB));  // open: Qn
  xor xor_4 (xor_4_out, INVB, BIN4);
  D_Flip_Flop d_ff_3 (.clk(LOAD), .D(xor_3_out), .Q(BOUT5), .preset(SETB), .en(ENB), .reset(CLRB));  // open: Qn
  xor xor_5 (xor_5_out, INVB, BIN3);
  D_Flip_Flop d_ff_4 (.clk(LOAD), .D(xor_4_out), .Q(BOUT4), .preset(SETB), .en(ENB), .reset(CLRB));  // open: Qn
  xor xor_6 (xor_6_out, INVB, BIN2);
  D_Flip_Flop d_ff_5 (.clk(LOAD), .D(xor_5_out), .Q(BOUT3), .preset(SETB), .en(ENB), .reset(CLRB));  // open: Qn
  xor xor_7 (xor_7_out, INVB, BIN1);
  D_Flip_Flop d_ff_6 (.clk(LOAD), .D(xor_6_out), .Q(BOUT2), .preset(SETB), .en(ENB), .reset(CLRB));  // open: Qn
  xor xor_8 (xor_8_out, INVB, BIN0);
  D_Flip_Flop d_ff_7 (.clk(LOAD), .D(xor_7_out), .Q(BOUT1), .preset(SETB), .en(ENB), .reset(CLRB));  // open: Qn
  D_Flip_Flop d_ff_8 (.clk(LOAD), .D(xor_8_out), .Q(BOUT0), .preset(SETB), .en(ENB), .reset(CLRB));  // open: Qn
endmodule

module ULA (
  input  PLUS1,
  input  B7,
  input  B6,
  input  B5,
  input  B4,
  input  B3,
  input  B2,
  input  B1,
  input  B0,
  input  INVB,
  input  INVA,
  input  A7,
  input  A6,
  input  A5,
  input  A4,
  input  A3,
  input  A2,
  input  A1,
  input  A0,
  input  INVO,
  output OVF,
  output S7,
  output S6,
  output S5,
  output S4,
  output S3,
  output S2,
  output S1,
  output S0
);

  wire somador_02_bits_2_cout, somador_02_bits_2_s, somador_02_bits_3_cout, somador_02_bits_3_s,
       somador_02_bits_4_cout, somador_02_bits_4_s, somador_02_bits_5_cout, somador_02_bits_5_s,
       somador_02_bits_6_cout, somador_02_bits_6_s, somador_02_bits_7_cout, somador_02_bits_7_s,
       somador_02_bits_8_cout, somador_02_bits_8_s, xor_2_out, xor_3_out, xor_5_out, xor_7_out, xor_8_out,
       xor_9_out, xor_11_out, xor_12_out, xor_14_out, xor_16_out, xor_17_out, xor_18_out, xor_20_out,
       xor_22_out, xor_23_out, xor_24_out;

  xor xor_1 (S7, OVF, INVO);
  xor xor_2 (xor_2_out, B7, INVB);
  Somador_02_bits somador_02_bits_1 (.Cout(OVF), .S(OVF), .Cin(somador_02_bits_2_cout), .B(xor_2_out), .A(xor_3_out));
  xor xor_3 (xor_3_out, A7, INVA);
  xor xor_4 (S6, somador_02_bits_2_s, INVO);
  xor xor_5 (xor_5_out, B6, INVB);
  Somador_02_bits somador_02_bits_2 (
    .Cout(somador_02_bits_2_cout), .S(somador_02_bits_2_s), .Cin(somador_02_bits_3_cout), .B(xor_5_out),
    .A(xor_7_out));
  xor xor_6 (S5, somador_02_bits_3_s, INVO);
  xor xor_7 (xor_7_out, A6, INVA);
  xor xor_8 (xor_8_out, B5, INVB);
  xor xor_9 (xor_9_out, A5, INVA);
  Somador_02_bits somador_02_bits_3 (
    .Cout(somador_02_bits_3_cout), .S(somador_02_bits_3_s), .Cin(somador_02_bits_4_cout), .B(xor_8_out),
    .A(xor_9_out));
  xor xor_10 (S4, somador_02_bits_4_s, INVO);
  xor xor_11 (xor_11_out, B4, INVB);
  Somador_02_bits somador_02_bits_4 (
    .Cout(somador_02_bits_4_cout), .S(somador_02_bits_4_s), .Cin(somador_02_bits_5_cout), .B(xor_11_out),
    .A(xor_12_out));
  xor xor_12 (xor_12_out, A4, INVA);
  xor xor_13 (S3, somador_02_bits_5_s, INVO);
  xor xor_14 (xor_14_out, B3, INVB);
  Somador_02_bits somador_02_bits_5 (
    .Cout(somador_02_bits_5_cout), .S(somador_02_bits_5_s), .Cin(somador_02_bits_6_cout), .B(xor_14_out),
    .A(xor_16_out));
  xor xor_15 (S2, somador_02_bits_6_s, INVO);
  xor xor_16 (xor_16_out, A3, INVA);
  xor xor_17 (xor_17_out, B2, INVB);
  xor xor_18 (xor_18_out, A2, INVA);
  Somador_02_bits somador_02_bits_6 (
    .Cout(somador_02_bits_6_cout), .S(somador_02_bits_6_s), .Cin(somador_02_bits_7_cout), .B(xor_17_out),
    .A(xor_18_out));
  xor xor_19 (S1, somador_02_bits_7_s, INVO);
  xor xor_20 (xor_20_out, B1, INVB);
  Somador_02_bits somador_02_bits_7 (
    .Cout(somador_02_bits_7_cout), .S(somador_02_bits_7_s), .Cin(somador_02_bits_8_cout), .B(xor_20_out),
    .A(xor_22_out));
  xor xor_21 (S0, somador_02_bits_8_s, INVO);
  xor xor_22 (xor_22_out, A1, INVA);
  xor xor_23 (xor_23_out, B0, INVB);
  Somador_02_bits somador_02_bits_8 (
    .Cout(somador_02_bits_8_cout), .S(somador_02_bits_8_s), .Cin(PLUS1), .B(xor_23_out), .A(xor_24_out));
  xor xor_24 (xor_24_out, A0, INVA);
endmodule
