// Logisim project meu-SAP1-7-.circ as structural Verilog: 12 circuits, main circuit main
module main (
  input  Ligar,
  input  in_2,
  output [3:0] W_MSB,
  output [3:0] W_LSB,
  output [5:0] out_5
);

  wire Clear, Clock, Clock_out, CP, Enable_A, Enable_CP, Enable_S, Halt, Load_A, Load_B, Load_O, Load_REM,
       nEnable_IR, nLoad_IR, not_1_out, not_2_out, Select_Adress, Subtract;
  wire [3:0] instructionregister_1_cs_output, memoryadressregister_1_output, O_LSB, O_MSB;
  wire [7:0] aregister_1_alu_output, bregister_1_output;

  MemoryAdressRegister memoryadressregister_1 (
    .Input(W_LSB), .Load(Load_REM), .Clock(Clock), .Output(memoryadressregister_1_output));
  not not_1 (not_1_out, Select_Adress);
  Controller_Sequencer controller_sequencer_1 (
    .Clock(Clock), .Clear(Clear), .Input_IR(instructionregister_1_cs_output), .Estado_T(out_5),
    .Palavra_de_Controle({CP, Enable_CP, Load_REM, Select_Adress, nLoad_IR, nEnable_IR, Load_A, Enable_A, Subtract, Enable_S, Load_B, Load_O}));
  ProgramCounter programcounter_1 (.Clock(Clock), .Count(CP), .Clear(Clear), .Enable(Enable_CP), .Output(W_LSB));
  RAM #(.addrWidth(4), .bus("separate")) ram_1 (
    .addr(memoryadressregister_1_output), .data({W_MSB, W_LSB}), .str(1'b0), .sel(not_1_out), .ld(1'b1),
    .clr(in_2));  // open: din, clk
  InstructionRegister instructionregister_1 (
    .Input({W_MSB, W_LSB}), .nLoad(nLoad_IR), .Clock(Clock), .Clear(Clear), .nEnable(nEnable_IR),
    .Bus_Output(W_LSB), .CS_Output(instructionregister_1_cs_output), .Halt(Halt));
  Adder_Subtractor adder_subtractor_1 (
    .B_Input(bregister_1_output), .Output({W_MSB, W_LSB}), .Subtract(Subtract), .Enable(Enable_S),
    .A_Input(aregister_1_alu_output));
  BRegister bregister_1 (.Input({W_MSB, W_LSB}), .Load(Load_B), .Clock(Clock), .Output(bregister_1_output));
  ARegister aregister_1 (
    .Bus_Output({W_MSB, W_LSB}), .Load(Load_A), .Clock(Clock), .Enable(Enable_A),
    .ALU_Output(aregister_1_alu_output), .Input({W_MSB, W_LSB}));
  OutputRegister outputregister_1 (
    .Input({W_MSB, W_LSB}), .Load(Load_O), .Clock(Clock), .Output({O_MSB, O_LSB}), .Clear(Clear));
  Hex_Digit_Display hex_digit_display_1 (.value(O_MSB));  // open: dp
  Hex_Digit_Display hex_digit_display_2 (.value(O_LSB));  // open: dp
  and and_1 (Clock, not_2_out, Ligar, Clock_out);
  not not_2 (not_2_out, Halt);
  Clock u_Clock (.out(Clock_out));
  not not_3 (Clear, Ligar);

  // Other names for the same wires on the sheet: Clear_RAM = in_2

  // Notes on the sheet:
  //   W-MSB
  //   W-LSB
  //   0000 - LDA
  //   0001 - ADD
  //   0010 - SUB
  //   1110 - OUT
  //   1111 - HLT
  //   Saída
  //   Instruções:
  //   Painel de Controle
endmodule

module ProgramCounter (
  input  Clock,
  input  Count,
  input  Clear,
  input  Enable,
  output [3:0] Output
);

  wire not_1_out;
  wire [3:0] counter_1_q;

  not not_1 (not_1_out, Clock);
  Counter #(.width(4), .max('hf)) counter_1 (
    .count(Count), .Q(counter_1_q), .clk(not_1_out), .clr(Clear));  // open: load, D, carry
  assign Output = Enable ? counter_1_q : 4'bz;  // Controlled_Buffer controlled_buffer_1
endmodule

module MemoryAdressRegister (
  input  [3:0] Input,
  input  Load,
  input  Clock,
  output [3:0] Output
);

  wire not_1_out;

  not not_1 (not_1_out, Load);
  Register #(.width(4)) register_1 (.D(Input), .en(not_1_out), .Q(Output), .clk(Clock));  // open: clr
endmodule

module InstructionRegister (
  input  [7:0] Input,
  input  nLoad,
  input  Clock,
  input  Clear,
  input  nEnable,
  output [3:0] Bus_Output,
  output [3:0] CS_Output,
  output Halt
);

  wire not_1_out, not_2_out;
  wire [3:0] register_1_q;

  not not_1 (not_1_out, nLoad);
  Register register_1 (.D(Input), .en(not_1_out), .Q({CS_Output, register_1_q}), .clk(Clock), .clr(Clear));
  not not_2 (not_2_out, nEnable);
  assign Bus_Output = not_2_out ? register_1_q : 4'bz;  // Controlled_Buffer controlled_buffer_1
  and and_1 (Halt, CS_Output[3], CS_Output[2], CS_Output[1], CS_Output[0]);
endmodule

module Controller_Sequencer (
  input  [3:0] Input_IR,
  input  Clock,
  input  Clear,
  output [5:0] Estado_T,
  output [11:0] Palavra_de_Controle
);

  wire not_1_out, or_1_out;
  wire [1:0] tstatesequencer_1_t6;
  wire [7:0] counter_1_q, multiplexer_1_out, rom_1_data;

  TStateSequencer tstatesequencer_1 (
    .Clock(Clock), .Clear(Clear), .Estado_T(Estado_T), .T3(tstatesequencer_1_t6[1]),
    .T6(tstatesequencer_1_t6[0]));
  ROM #(.addrWidth(4)) rom_1 (.addr(Input_IR), .data(rom_1_data));  // open: sel
  or or_1 (or_1_out, tstatesequencer_1_t6[1], tstatesequencer_1_t6[0]);
  not not_1 (not_1_out, or_1_out);
  Multiplexer #(.select(2), .width(8), .enable("false")) multiplexer_1 (
    .in1({8{1'b0}}), .in2(rom_1_data), .out(multiplexer_1_out), .sel(tstatesequencer_1_t6));  // open: in0, in3
  Counter #(.trigger("falling")) counter_1 (
    .load(or_1_out), .D(multiplexer_1_out), .count(not_1_out), .Q(counter_1_q), .clk(Clock), .clr(Clear));  // open: carry
  ROM #(.dataWidth(12)) rom_2 (.addr(counter_1_q), .data(Palavra_de_Controle));  // open: sel

  // Notes on the sheet:
  //   contents of rom_1 (hex, n*v repeats v):
  //   3 6 9 f 12 15 18 7*0 c
  //   contents of rom_2 (hex, n*v repeats v):
  //   5e3 be3 263 1a3 2c3 3e3 1a3 2e1 3c7 1a3 2e1 3cf 3f2 3e3 3e3 9*0 1a3 e3 2c3
endmodule

module TStateSequencer (
  input  Clock,
  input  Clear,
  output [5:0] Estado_T,
  output T3,
  output T6
);

  wire not_1_out;

  not not_1 (not_1_out, Clock);
  D_Flip_Flop d_ff_1 (.clk(not_1_out), .D(Estado_T[0]), .Q(Estado_T[5]), .preset(Clear));  // open: Qn, en, reset
  D_Flip_Flop d_ff_2 (.clk(not_1_out), .D(Estado_T[5]), .Q(Estado_T[4]), .reset(Clear));  // open: Qn, preset, en
  D_Flip_Flop d_ff_3 (.clk(not_1_out), .D(Estado_T[4]), .Q(Estado_T[3]), .reset(Clear));  // open: Qn, preset, en
  D_Flip_Flop d_ff_4 (.clk(not_1_out), .D(Estado_T[3]), .Q(Estado_T[2]), .reset(Clear));  // open: Qn, preset, en
  D_Flip_Flop d_ff_5 (.clk(not_1_out), .D(Estado_T[2]), .Q(Estado_T[1]), .reset(Clear));  // open: Qn, preset, en
  D_Flip_Flop d_ff_6 (.clk(not_1_out), .D(Estado_T[1]), .Q(Estado_T[0]), .reset(Clear));  // open: Qn, preset, en

  assign T3 = Estado_T[3];
  assign T6 = Estado_T[0];
endmodule

module ARegister (
  input  [7:0] Input,
  input  Load,
  input  Clock,
  input  Enable,
  output [7:0] Bus_Output,
  output [7:0] ALU_Output
);

  wire not_1_out;

  Register register_1 (.D(Input), .en(not_1_out), .Q(ALU_Output), .clk(Clock));  // open: clr
  not not_1 (not_1_out, Load);
  assign Bus_Output = Enable ? ALU_Output : 8'bz;  // Controlled_Buffer controlled_buffer_1
endmodule

module BRegister (
  input  [7:0] Input,
  input  Load,
  input  Clock,
  output [7:0] Output
);

  wire not_1_out;

  not not_1 (not_1_out, Load);
  Register register_1 (.D(Input), .en(not_1_out), .Q(Output), .clk(Clock));  // open: clr
endmodule

module Adder_Subtractor (
  input  [7:0] A_Input,
  input  [7:0] B_Input,
  input  Subtract,
  input  Enable,
  output [7:0] Output
);

  wire adder_1_cout;
  wire [7:0] adder_1_out, xor_1_out;

  assign xor_1_out = B_Input ^ {8{Subtract}};  // XOR_Gate xor_1, 8 bits wide
  Adder adder_1 (.a(xor_1_out), .b(A_Input), .out(adder_1_out), .cin(Subtract), .cout(adder_1_cout));
  assign Output = Enable ? adder_1_out : 8'bz;  // Controlled_Buffer controlled_buffer_1
endmodule

module OutputRegister (
  input  [7:0] Input,
  input  Load,
  input  Clock,
  input  Clear,
  output [7:0] Output
);

  wire not_1_out;

  not not_1 (not_1_out, Load);
  Register register_1 (.D(Input), .en(not_1_out), .Q(Output), .clk(Clock), .clr(Clear));
endmodule

module Transmission (
  input  [7:0] Output,
  input  [7:0] RX,
  input  Shift,
  input  Clock,
  output [7:0] TX,
  output [7:0] Input
);

  Shift_Register #(.width(8)) Transmissor (
    .shift(Shift), .in(Output), .clk(Clock), .out(TX));  // open: load, clr, d0, q0, d1, q1, d2, q2, d3, q3, d4, q4, d5, q5, d6, q6, d7, q7
  Shift_Register #(.width(8)) Receptor (
    .shift(Shift), .in(RX), .clk(Clock), .out(Input));  // open: load, clr, d0, q0, d1, q1, d2, q2, d3, q3, d4, q4, d5, q5, d6, q6, d7, q7

  // Other names for the same wires on the sheet: Entrada[7:0] = Output
endmodule

module TesteTransmissao (
  input  [7:0] in_1,
  output [7:0] out_2,
  output [7:0] out_3
);

  wire clock_1_out, counter_2_carry;
  wire [7:0] counter_1_q, ram_1_data, transmission_1_tx, transmission_2_tx;

  Clock clock_1 (.out(clock_1_out));
  Counter counter_1 (.Q(counter_1_q), .clk(counter_2_carry));  // open: load, D, count, carry, clr
  Counter #(.max('h8)) counter_2 (.carry(counter_2_carry), .clk(clock_1_out));  // open: load, D, count, Q, clr
  RAM ram_1 (.addr(counter_1_q), .data(ram_1_data), .sel(clock_1_out), .clk(clock_1_out));  // open: ld, clr
  Transmission transmission_1 (
    .Output(ram_1_data), .Input(out_3), .Shift(clock_1_out), .Clock(clock_1_out), .TX(transmission_1_tx),
    .RX(transmission_2_tx));
  Transmission transmission_2 (
    .Output(in_1), .Input(out_2), .Shift(clock_1_out), .Clock(clock_1_out), .TX(transmission_2_tx),
    .RX(transmission_1_tx));
endmodule
