# Fritzing sketch contador (saved by Fritzing 0.9.3b)
circuit board: 5.5cm x 10cm
breadboards: 1

parts:
  Grove1 = Grove 4 Digit Display
  R7 = Resistor [tolerance=±5% resistance=100k package=THT]
  R3 = Resistor [tolerance=±5% resistance=1k package=THT]
  R5 = Resistor [tolerance=±5% resistance=100k package=THT]
  R6 = Resistor [tolerance=±5% resistance=100k package=THT]
  R2 = Resistor [tolerance=±5% resistance=1k package=THT]
  R1 = Resistor [tolerance=±5% resistance=1k package=THT]
  S3 = Pushbutton [package="[THT]"]
  S1 = Pushbutton [package="[THT]"]
  S2 = Pushbutton [package="[THT]"]
  U1 = NodeMCU V1.0
  LED1 = LED - 5mm [color="Red (633nm)" package="5 mm [THT]"]
  R8 = Resistor [tolerance=±5% resistance=220 package=THT]
  BAT3 = Battery Holders [package=battery-aaa]
  BAT2 = Battery Holders [package=battery-aaa]
  BAT1 = Battery Holders [package=battery-aaa]
  S4 = Momentary Switch [package=ksa_sealed_tac_switch]

nets:
  GND: Grove1.GND, R7.Pin_1, R5.Pin_1, R6.Pin_1, U1.GND, LED1.cathode, S4.4
  VCC: Grove1.VCC, R3.Pin_0, R2.Pin_0, R1.Pin_0, U1.Vin, BAT3.+
  N1: Grove1.DIO, U1.D6
  N2: Grove1.CLK, U1.D2
  N3: R7.Pin_0, S1.Pin_1, S1.Pin_2, U1.D0
  N4: R3.Pin_1, S3.Pin_3, S3.Pin_4
  N5: R5.Pin_0, S3.Pin_1, S3.Pin_2, U1.D8
  N6: R6.Pin_0, S2.Pin_1, S2.Pin_2, U1.D1
  N7: R2.Pin_1, S2.Pin_3, S2.Pin_4
  N8: R1.Pin_1, S1.Pin_3, S1.Pin_4
  N9: U1.D4, R8.Pin_1
  N10: LED1.anode, R8.Pin_0
  N11: BAT3.-, BAT2.+
  N12: BAT2.-, BAT1.+
  N13: BAT1.-, S4.1

custom parts:
  NodeMCU V1.0: ESP8266 based NodeMCU
